// Logisim project half_adder.circ as structural Verilog: 2 circuits, main circuit main
module main (
  input  A,
  input  B,
  input  C,
  output out_4
);

  // half_adder half_adder_1: pin names not known; wires that end beside it: A, B, C, out_4
endmodule

module half_adder (
  input  entrada_A,
  input  entrada_B,
  output SUM,
  output CARRY
);

  xor XOR1 (SUM, entrada_A, entrada_B);
  and AND1 (CARRY, entrada_A, entrada_B);
endmodule
