// Logisim project basic_logic_gates.circ as structural Verilog: 2 circuits, main circuit logic_gates
module main (
  input  in_1,
  input  in_2,
  output out_3,
  output out_4,
  output out_5,
  output out_6,
  output out_7,
  output out_8,
  output out_9
);

  logic_gates logic_gates_1 (
    .entrada_A(in_1), .entrada_B(in_2), .salida_1(out_3), .salida_2(out_4), .salida_3(out_5),
    .salida_4(out_6), .salida_5(out_7), .salida_6(out_8), .salida_7(out_9));
endmodule

module logic_gates (
  input  entrada_A,
  input  entrada_B,
  output salida_1,
  output salida_2,
  output salida_3,
  output salida_4,
  output salida_5,
  output salida_6,
  output salida_7
);

  not NOT (salida_1, entrada_A);
  and AND1 (salida_2, entrada_A, entrada_B);
  or OR1 (salida_3, entrada_A, entrada_B);
  xor XOR1 (salida_4, entrada_A, entrada_B);
  nand NAND1 (salida_5, entrada_A, entrada_B);
  nor NOR1 (salida_6, entrada_A, entrada_B);
  xnor XNOR1 (salida_7, entrada_A, entrada_B);

  // Notes on the sheet:
  //   salida_1=entrada_A'
  //   salida_2=entrada_B * entrada_C
  //   salida_3=entrada_D + entrada_E
  //   salida_4=entrada_F XOR entrada_G
  //   salida_5=(entrada_A * entrada_B)'
  //   salida_6=(entrada_A + entrada_B)'
  //   salida_7=(entrada_A XOR entrada_B)'
endmodule
