// Logisim project boolean_logic.circ as structural Verilog: 2 circuits, main circuit main
module main (
  input  A,
  input  B,
  input  C,
  output out_4
);

  equation_1 equation_1_1 (.entrada_A(A), .entrada_B(B), .entrada_C(C), .salida_1(out_4));
endmodule

module equation_1 (
  input  entrada_A,
  input  entrada_B,
  input  entrada_C,
  output salida_1
);

  wire AND1_out, AND2_out, AND3_out;

  and AND1 (AND1_out, ~entrada_A, entrada_B, ~entrada_C);  // AND_Gate
  and AND2 (AND2_out, entrada_A, ~entrada_B, ~entrada_C);  // AND_Gate
  and AND3 (AND3_out, entrada_A, entrada_B, entrada_C);
  or OR1 (salida_1, AND1_out, AND2_out, AND3_out);

  // Notes on the sheet:
  //   (A'BC')+(AB'C')+(ABC)
endmodule
